// Logisim project computer.circ as structural Verilog: 10 circuits, main circuit main
// CC
module main (
  input  in_1,
  input  in_2,
  input  in_3,
  input  in_4,
  input  in_5,
  output [6:0] out_6,
  output out_7
);

  wire AI, AO, BI, BO, button_1_out, CCl, CI, CLK, clock_1_out, CO, DI, DO, EO, FI, HLT, IE, II, MI,
       not_1_out, OI, or_1_out, R, RI, RO, SP;
  wire [1:0] AB;
  wire [2:0] cc_1_q;
  wire [3:0] PCP, SPP;
  wire [6:0] alu_1_flags, ALUP, Flags;
  wire [7:4] cu_1_q2;
  wire [15:0] alu_1_q, count_1_q, ram_1_dout, register_1_q, regs_1_out_6, regs_3_out_6, regs_4_out_6;
  wire [23:0] sevensegdriver_1_down, sevensegdriver_1_up;

  Keyboard keyboard_1 (.clk(in_1), .re(in_4), .clr(in_5), .avail(out_7), .data(out_6));
  Clock clock_1 (.out(clock_1_out));
  not not_1 (not_1_out, HLT);
  Register #(.width(16)) register_1 (.D(count_1_q), .en(MI), .Q(register_1_q), .clk(CLK), .clr(R));
  RAM #(.addrWidth(16), .asyncread("true"), .dataWidth(16)) ram_1 (
    .addr(register_1_q), .we(RI), .oe(1'b1), .clk(CLK), .din(count_1_q), .dout(ram_1_dout));
  REGS regs_1 (.IE(II), .CLK(CLK), .R(R), .D(count_1_q), .out_6(regs_1_out_6));  // open: OE, O
  CC cc_1 (.R(R), .nCLK(CLK), .Q(cc_1_q));
  and and_1 (CLK, clock_1_out, not_1_out);
  COUNT count_1 (.JInEO(SPP), .R(R), .CLK(CLK), .D(count_1_q), .Q(count_1_q));
  REGS regs_2 (.IE(DI), .CLK(CLK), .R(R), .D(count_1_q), .OE(DO), .O(count_1_q));  // open: out_6
  CU cu_1 (
    .T(cc_1_q), .F(Flags), .I(regs_1_out_6[7:0]), .QALU(ALUP),
    .Q1({CI, SP, IE, OI, II, RO, RI, MI, SPP, PCP, HLT, AB, BO, BI, AO, AI, EO, FI}),
    .Q2({cu_1_q2, CO, DO, DI, CCl}));
  COUNT count_2 (.JInEO(PCP), .R(R), .CLK(CLK), .D(count_1_q), .Q(count_1_q));
  assign count_1_q = RO ? ram_1_dout : 16'bz;  // Controlled_Buffer controlled_buffer_1
  Console console_1 (.OE(CO), .IE(IE), .CLK(CLK), .SP(SP), .R(or_1_out), .Push(CI), .D(count_1_q));
  REGS regs_3 (.IE(AI), .CLK(CLK), .R(R), .D(count_1_q), .OE(AO), .out_6(regs_3_out_6), .O(count_1_q));
  ALU alu_1 (.AB(AB), .A(regs_3_out_6), .B(regs_4_out_6), .Sel(ALUP), .Flags(alu_1_flags), .Q(alu_1_q));
  REGS regs_4 (.IE(BI), .CLK(CLK), .R(R), .D(count_1_q), .OE(BO), .out_6(regs_4_out_6), .O(count_1_q));
  _7_Segment_Display u_7_segment_display_1 (
    .g(sevensegdriver_1_up[23]), .f(sevensegdriver_1_up[22]), .a(sevensegdriver_1_up[21]),
    .b(sevensegdriver_1_up[20]), .e(sevensegdriver_1_down[23]), .d(sevensegdriver_1_down[22]),
    .c(sevensegdriver_1_down[21]), .dp(sevensegdriver_1_down[20]));
  SevenSegDriver sevensegdriver_1 (
    .OI(OI), .CLK(CLK), .R(R), .S(button_1_out), .D(count_1_q), .down(sevensegdriver_1_down),
    .up(sevensegdriver_1_up));
  Button button_1 (.out(button_1_out));
  or or_1 (or_1_out, CCl, R);
  // Probe on alu_1_q
  assign count_1_q = EO ? alu_1_q : 16'bz;  // Controlled_Buffer controlled_buffer_2
  Register #(.width(7)) register_2 (.D(alu_1_flags), .en(FI), .Q(Flags), .clk(CLK), .clr(R));
  _7_Segment_Display u_7_segment_display_2 (
    .g(sevensegdriver_1_up[19]), .f(sevensegdriver_1_up[18]), .a(sevensegdriver_1_up[17]),
    .b(sevensegdriver_1_up[16]), .e(sevensegdriver_1_down[19]), .d(sevensegdriver_1_down[18]),
    .c(sevensegdriver_1_down[17]), .dp(sevensegdriver_1_down[16]));
  _7_Segment_Display u_7_segment_display_3 (
    .g(sevensegdriver_1_up[15]), .f(sevensegdriver_1_up[14]), .a(sevensegdriver_1_up[13]),
    .b(sevensegdriver_1_up[12]), .e(sevensegdriver_1_down[15]), .d(sevensegdriver_1_down[14]),
    .c(sevensegdriver_1_down[13]), .dp(sevensegdriver_1_down[12]));
  Button button_2 (.out(R));
  _7_Segment_Display u_7_segment_display_4 (
    .g(sevensegdriver_1_up[11]), .f(sevensegdriver_1_up[10]), .a(sevensegdriver_1_up[9]),
    .b(sevensegdriver_1_up[8]), .e(sevensegdriver_1_down[11]), .d(sevensegdriver_1_down[10]),
    .c(sevensegdriver_1_down[9]), .dp(sevensegdriver_1_down[8]));
  _7_Segment_Display u_7_segment_display_5 (
    .g(sevensegdriver_1_up[7]), .f(sevensegdriver_1_up[6]), .a(sevensegdriver_1_up[5]),
    .b(sevensegdriver_1_up[4]), .e(sevensegdriver_1_down[7]), .d(sevensegdriver_1_down[6]),
    .c(sevensegdriver_1_down[5]), .dp(sevensegdriver_1_down[4]));
  _7_Segment_Display u_7_segment_display_6 (
    .g(sevensegdriver_1_up[3]), .f(sevensegdriver_1_up[2]), .a(sevensegdriver_1_up[1]),
    .b(sevensegdriver_1_up[0]), .e(sevensegdriver_1_down[3]), .d(sevensegdriver_1_down[2]),
    .c(sevensegdriver_1_down[1]), .dp(sevensegdriver_1_down[0]));
endmodule

module SevenSegDriver (
  input  [15:0] D,
  input  OI,
  input  CLK,
  input  R,
  input  S,
  output [23:0] down,
  output [23:0] up
);

  wire [15:0] register_1_q;

  Register #(.width(16)) register_1 (.D(D), .en(OI), .clk(CLK), .Q(register_1_q), .clr(R));
  ROM #(.addrWidth(20)) rom_1 (.addr({S, 3'b000, register_1_q}), .data({up[3:0], down[3:0]}));
  ROM #(.addrWidth(20)) rom_2 (.addr({S, 3'b001, register_1_q}), .data({up[7:4], down[7:4]}));
  ROM #(.addrWidth(20)) rom_3 (.addr({S, 3'b010, register_1_q}), .data({up[11:8], down[11:8]}));
  ROM #(.addrWidth(20)) rom_4 (.addr({S, 3'b011, register_1_q}), .data({up[15:12], down[15:12]}));
  ROM #(.addrWidth(20)) rom_5 (.addr({S, 3'b100, register_1_q}), .data({up[19:16], down[19:16]}));

  assign down[23:20] = 4'b0000;
  assign up[23:20] = {S, 3'b000};

  // Notes on the sheet:
  //   contents of rom_1 (hex, n*v repeats v):
  //   7e 12 bc b6 d2 e6 ee 32 fe f6 7e 12 bc b6 d2 e6 ee 32 fe f6 7e 12 bc b6 d2 e6 ee 32 fe f6 7e 12 bc
  //   b6 d2 e6 ee 32 fe f6 7e 12 bc b6 d2 e6 ee 32 fe f6 7e 12 bc b6 d2 e6 ee 32 fe f6 7e 12 bc b6 d2 e6
  //   ee 32 fe f6 7e 12 bc b6 d2 e6 ee 32 fe f6 7e 12 bc b6 d2 e6 ee 32 fe f6 7e 12 bc b6 d2 e6 ee 32 fe
  //   f6 7e 12 bc b6 d2 e6 ee 32 fe f6 7e 12 bc b6 d2 e6 ee 32 fe f6 7e 12 bc b6 d2 e6 ee 32 fe f6 7e 12
  //   bc b6 d2 e6 ee 32 fe f6 7e 12 bc b6 d2 e6 ee 32 fe f6 7e 12 bc b6 d2 e6 ee 32 fe f6 7e 12 bc b6 d2
  //   e6 ee 32 fe f6 7e 12 bc b6 d2 e6 ee 32 fe f6 7e 12 bc b6 d2 e6 ee 32 fe f6 7e 12 bc b6 d2 e6 ee 32
  //   fe f6 7e 12 bc b6 d2 e6 ee 32 fe f6 7e 12 bc b6 d2 e6 ee 32 fe f6 7e 12 bc b6 d2 e6 ee 32 fe f6 7e
  //   12 bc b6 d2 e6 ee 32 fe f6 7e 12 bc b6 d2 e6 ee 32 fe f6 7e 12 bc b6 d2 e6 ee 32 fe f6 7e 12 bc b6
  //   d2 e6 ee 32 fe f6 7e 12 bc b6 d2 e6 ee 32 fe f6 7e 12 bc b6 d2 e6 ee 32 fe f6 7e 12 bc b6 d2 e6 ee
  //   32 fe f6 7e 12 bc b6 d2 e6 ee 32 fe f6 7e 12 bc b6 d2 e6 ee 32 fe f6 7e 12 bc b6 d2 e6 ee 32 fe f6
  //   7e 12 bc b6 d2 e6 ee 32 fe f6 7e 12 bc b6 d2 e6 ee 32 fe f6 7e 12 bc b6 d2 e6 ee 32 fe f6 7e 12 bc
  //   b6 d2 e6 ee 32 fe f6 7e 12 bc b6 d2 e6 ee 32 fe f6 7e 12 bc b6 d2 e6 ee 32 fe f6 7e 12 bc b6 d2 e6
  //   ee 32 fe f6 7e 12 bc b6 d2 e6 ee 32 fe f6 7e 12 bc b6 d2 e6 ee 32 fe f6 7e 12 bc b6 d2 e6 ee 32 fe
  //   f6 7e 12 bc b6 d2 e6 ee 32 fe f6 7e 12 bc b6 d2 e6 ee 32 fe f6 7e 12 bc b6 d2 e6 ee 32 fe f6 7e 12
  //   bc b6 d2 e6 ee 32 fe f6 7e 12 bc b6 d2 e6 ee 32 fe f6 7e 12 bc b6 d2 e6 ee 32 fe f6 7e 12 bc b6 d2
  //   e6 ee 32 fe f6 7e 12 bc b6 d2 e6 ee 32 fe f6 7e 12 bc b6 d2 e6 ee 32 fe f6 7e 12 bc b6 d2 e6 ee 32
  //   fe f6 7e 12 bc b6 d2 e6 ee 32 fe f6 7e 12 bc b6 d2 e6 ee 32 fe f6 7e 12 bc b6 d2 e6 ee 32 fe f6 7e
  //   12 bc b6 d2 e6 ee 32 fe f6 7e 12 bc b6 d2 e6 ee 32 fe f6 7e 12 bc b6 d2 e6 ee 32 fe f6 7e 12 bc b6
  //   d2 e6 ee 32 fe f6 7e 12 bc b6 d2 e6 ee 32 fe f6 7e 12 bc b6 d2 e6 ee 32 fe f6 7e 12 bc b6 d2 e6 ee
  //   32 fe f6 7e 12 bc b6 d2 e6 ee 32 fe f6 7e 12 bc b6 d2 e6 ee 32 fe f6 7e 12 bc b6 d2 e6 ee 32 fe f6
  //   7e 12 bc b6 d2 e6 ee 32 fe f6 7e 12 bc b6 d2 e6 ee 32 fe f6 7e 12 bc b6 d2 e6 ee 32 fe f6 7e 12 bc
  //   b6 d2 e6 ee 32 fe f6 7e 12 bc b6 d2 e6 ee 32 fe f6 7e 12 bc b6 d2 e6 ee 32 fe f6 7e 12 bc b6 d2 e6
  //   ee 32 fe f6 7e 12 bc b6 d2 e6 ee 32 fe f6 7e 12 bc b6 d2 e6 ee 32 fe f6 7e 12 bc b6 d2 e6 ee 32 fe
  //   f6 7e 12 bc b6 d2 e6 ee 32 fe f6 7e 12 bc b6 d2 e6 ee 32 fe f6 7e 12 bc b6 d2 e6 ee 32 fe f6 7e 12
  //   bc b6 d2 e6 ee 32 fe f6 7e 12 bc b6 d2 e6 ee 32 fe f6 7e 12 bc b6 d2 e6 ee 32 fe f6 7e 12 bc b6 d2
  //   e6 ee 32 fe f6 7e 12 bc b6 d2 e6 ee 32 fe f6 7e 12 bc b6 d2 e6 ee 32 fe f6 7e 12 bc b6 d2 e6 ee 32
  //   fe f6 7e 12 bc b6 d2 e6 ee 32 fe f6 7e 12 bc b6 d2 e6 ee 32 fe f6 7e 12 bc b6 d2 e6 ee 32 fe f6 7e
  //   12 bc b6 d2 e6 ee 32 fe f6 7e 12 bc b6 d2 e6 ee 32 fe f6 7e 12 bc b6 d2 e6 ee 32 fe f6 7e 12 bc b6
  //   d2 e6 ee 32 fe f6 7e 12 bc b6 d2 e6 ee 32 fe f6 7e 12 bc b6 d2 e6 ee 32 fe f6 7e 12 bc b6 d2 e6 ee
  //   32 fe f6 7e 12 bc b6 d2 e6 ee 32 fe f6 7e 12 bc b6 d2 e6 ee 32 fe f6 7e 12 bc b6 d2 e6 ee 32 fe f6
  //   7e 12 bc b6 d2 e6 ee 32 fe f6 7e 12 bc b6 d2 e6 ee 32 fe f6 7e 12 bc b6 d2 e6 ee 32 fe f6 7e 12 bc
  //   b6 d2 e6 ee 32 fe f6 7e 12 bc b6 d2 e6 ee 32 fe f6 7e 12 bc b6 d2 e6 ee 32 fe f6 7e 12 bc b6 d2 e6
  //   ee 32 fe f6 7e 12 bc b6 d2 e6 ee 32 fe f6 7e 12 bc b6 d2 e6 ee 32 fe f6 7e 12 bc b6 d2 e6 ee 32 fe
  //   f6 7e 12 bc b6 d2 e6 ee 32 fe f6 7e 12 bc b6 d2 e6 ee 32 fe f6 7e 12 bc b6 d2 e6 ee 32 fe f6 7e 12
  //   bc b6 d2 e6 ee 32 fe f6 7e 12 bc b6 d2 e6 ee 32 fe f6 7e 12 bc b6 d2 e6 ee 32 fe f6 7e 12 bc b6 d2
  //   e6 ee 32 fe f6 7e 12 bc b6 d2 e6 ee 32 fe f6 7e 12 bc b6 d2 e6 ee 32 fe f6 7e 12 bc b6 d2 e6 ee 32
  //   fe f6 7e 12 bc b6 d2 e6 ee 32 fe f6 7e 12 bc b6 d2 e6 ee 32 fe f6 7e 12 bc b6 d2 e6 ee 32 fe f6 7e
  //   12 bc b6 d2 e6 ee 32 fe f6 7e 12 bc b6 d2 e6 ee 32 fe f6 7e 12 bc b6 d2 e6 ee 32 fe f6 7e 12 bc b6
  //   d2 e6 ee 32 fe f6 7e 12 bc b6 d2 e6 ee 32 fe f6 7e 12 bc b6 d2 e6 ee 32 fe f6 7e 12 bc b6 d2 e6 ee
  //   32 fe f6 7e 12 bc b6 d2 e6 ee 32 fe f6 7e 12 bc b6 d2 e6 ee 32 fe f6 7e 12 bc b6 d2 e6 ee 32 fe f6
  //   7e 12 bc b6 d2 e6 ee 32 fe f6 7e 12 bc b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
  //   contents of rom_2 (hex, n*v repeats v):
  //   7e 12 bc b6 d2 e6 ee 32 fe f6 7e 12 bc b6 d2 e6 ee 32 fe f6 7e 12 bc b6 d2 e6 ee 32 fe f6 7e 12 bc
  //   b6 d2 e6 ee 32 fe f6 7e 12 bc b6 d2 e6 ee 32 fe f6 7e 12 bc b6 d2 e6 ee 32 fe f6 7e 12 bc b6 d2 e6
  //   ee 32 fe f6 7e 12 bc b6 d2 e6 ee 32 fe f6 7e 12 bc b6 d2 e6 ee 32 fe f6 7e 12 bc b6 d2 e6 ee 32 fe
  //   f6 7e 12 bc b6 d2 e6 ee 32 fe f6 7e 12 bc b6 d2 e6 ee 32 fe f6 7e 12 bc b6 d2 e6 ee 32 fe f6 7e 12
  //   bc b6 d2 e6 ee 32 fe f6 7e 12 bc b6 d2 e6 ee 32 fe f6 7e 12 bc b6 d2 e6 ee 32 fe f6 7e 12 bc b6 d2
  //   e6 ee 32 fe f6 7e 12 bc b6 d2 e6 ee 32 fe f6 7e 12 bc b6 d2 e6 ee 32 fe f6 7e 12 bc b6 d2 e6 ee 32
  //   fe f6 7e 12 bc b6 d2 e6 ee 32 fe f6 7e 12 bc b6 d2 e6 ee 32 fe f6 7e 12 bc b6 d2 e6 ee 32 fe f6 7e
  //   12 bc b6 d2 e6 ee 32 fe f6 7e 12 bc b6 d2 e6 ee 32 fe f6 7e 12 bc b6 d2 e6 ee 32 fe f6 7e 12 bc b6
  //   d2 e6 ee 32 fe f6 7e 12 bc b6 d2 e6 ee 32 fe f6 7e 12 bc b6 d2 e6 ee 32 fe f6 7e 12 bc b6 d2 e6 ee
  //   32 fe f6 7e 12 bc b6 d2 e6 ee 32 fe f6 7e 12 bc b6 d2 e6 ee 32 fe f6 7e 12 bc b6 d2 e6 ee 32 fe f6
  //   7e 12 bc b6 d2 e6 ee 32 fe f6 7e 12 bc b6 d2 e6 ee 32 fe f6 7e 12 bc b6 d2 e6 ee 32 fe f6 7e 12 bc
  //   b6 d2 e6 ee 32 fe f6 7e 12 bc b6 d2 e6 ee 32 fe f6 7e 12 bc b6 d2 e6 ee 32 fe f6 7e 12 bc b6 d2 e6
  //   ee 32 fe f6 7e 12 bc b6 d2 e6 ee 32 fe f6 7e 12 bc b6 d2 e6 ee 32 fe f6 7e 12 bc b6 d2 e6 ee 32 fe
  //   f6 7e 12 bc b6 d2 e6 ee 32 fe f6 7e 12 bc b6 d2 e6 ee 32 fe f6 7e 12 bc b6 d2 e6 ee 32 fe f6 7e 12
  //   bc b6 d2 e6 ee 32 fe f6 7e 12 bc b6 d2 e6 ee 32 fe f6 7e 12 bc b6 d2 e6 ee 32 fe f6 7e 12 bc b6 d2
  //   e6 ee 32 fe f6 7e 12 bc b6 d2 e6 ee 32 fe f6 7e 12 bc b6 d2 e6 ee 32 fe f6 7e 12 bc b6 d2 e6 ee 32
  //   fe f6 7e 12 bc b6 d2 e6 ee 32 fe f6 7e 12 bc b6 d2 e6 ee 32 fe f6 7e 12 bc b6 d2 e6 ee 32 fe f6 7e
  //   12 bc b6 d2 e6 ee 32 fe f6 7e 12 bc b6 d2 e6 ee 32 fe f6 7e 12 bc b6 d2 e6 ee 32 fe f6 7e 12 bc b6
  //   d2 e6 ee 32 fe f6 7e 12 bc b6 d2 e6 ee 32 fe f6 7e 12 bc b6 d2 e6 ee 32 fe f6 7e 12 bc b6 d2 e6 ee
  //   32 fe f6 7e 12 bc b6 d2 e6 ee 32 fe f6 7e 12 bc b6 d2 e6 ee 32 fe f6 7e 12 bc b6 d2 e6 ee 32 fe f6
  //   7e 12 bc b6 d2 e6 ee 32 fe f6 7e 12 bc b6 d2 e6 ee 32 fe f6 7e 12 bc b6 d2 e6 ee 32 fe f6 7e 12 bc
  //   b6 d2 e6 ee 32 fe f6 7e 12 bc b6 d2 e6 ee 32 fe f6 7e 12 bc b6 d2 e6 ee 32 fe f6 7e 12 bc b6 d2 e6
  //   ee 32 fe f6 7e 12 bc b6 d2 e6 ee 32 fe f6 7e 12 bc b6 d2 e6 ee 32 fe f6 7e 12 bc b6 d2 e6 ee 32 fe
  //   f6 7e 12 bc b6 d2 e6 ee 32 fe f6 7e 12 bc b6 d2 e6 ee 32 fe f6 7e 12 bc b6 d2 e6 ee 32 fe f6 7e 12
  //   bc b6 d2 e6 ee 32 fe f6 7e 12 bc b6 d2 e6 ee 32 fe f6 7e 12 bc b6 d2 e6 ee 32 fe f6 7e 12 bc b6 d2
  //   e6 ee 32 fe f6 7e 12 bc b6 d2 e6 ee 32 fe f6 7e 12 bc b6 d2 e6 ee 32 fe f6 7e 12 bc b6 d2 e6 ee 32
  //   fe f6 7e 12 bc b6 d2 e6 ee 32 fe f6 7e 12 bc b6 d2 e6 ee 32 fe f6 7e 12 bc b6 d2 e6 ee 32 fe f6 7e
  //   12 bc b6 d2 e6 ee 32 fe f6 7e 12 bc b6 d2 e6 ee 32 fe f6 7e 12 bc b6 d2 e6 ee 32 fe f6 7e 12 bc b6
  //   d2 e6 ee 32 fe f6 7e 12 bc b6 d2 e6 ee 32 fe f6 7e 12 bc b6 d2 e6 ee 32 fe f6 7e 12 bc b6 d2 e6 ee
  //   32 fe f6 7e 12 bc b6 d2 e6 ee 32 fe f6 7e 12 bc b6 d2 e6 ee 32 fe f6 7e 12 bc b6 d2 e6 ee 32 fe f6
  //   7e 12 bc b6 d2 e6 ee 32 fe f6 7e 12 bc b6 d2 e6 ee 32 fe f6 7e 12 bc b6 d2 e6 ee 32 fe f6 7e 12 bc
  //   b6 d2 e6 ee 32 fe f6 7e 12 bc b6 d2 e6 ee 32 fe f6 7e 12 bc b6 d2 e6 ee 32 fe f6 7e 12 bc b6 d2 e6
  //   ee 32 fe f6 7e 12 bc b6 d2 e6 ee 32 fe f6 7e 12 bc b6 d2 e6 ee 32 fe f6 7e 12 bc b6 d2 e6 ee 32 fe
  //   f6 7e 12 bc b6 d2 e6 ee 32 fe f6 7e 12 bc b6 d2 e6 ee 32 fe f6 7e 12 bc b6 d2 e6 ee 32 fe f6 7e 12
  //   bc b6 d2 e6 ee 32 fe f6 7e 12 bc b6 d2 e6 ee 32 fe f6 7e 12 bc b6 d2 e6 ee 32 fe f6 7e 12 bc b6 d2
  //   e6 ee 32 fe f6 7e 12 bc b6 d2 e6 ee 32 fe f6 7e 12 bc b6 d2 e6 ee 32 fe f6 7e 12 bc b6 d2 e6 ee 32
  //   fe f6 7e 12 bc b6 d2 e6 ee 32 fe f6 7e 12 bc b6 d2 e6 ee 32 fe f6 7e 12 bc b6 d2 e6 ee 32 fe f6 7e
  //   12 bc b6 d2 e6 ee 32 fe f6 7e 12 bc b6 d2 e6 ee 32 fe f6 7e 12 bc b6 d2 e6 ee 32 fe f6 7e 12 bc b6
  //   d2 e6 ee 32 fe f6 7e 12 bc b6 d2 e6 ee 32 fe f6 7e 12 bc b6 d2 e6 ee 32 fe f6 7e 12 bc b6 d2 e6 ee
  //   32 fe f6 7e 12 bc b6 d2 e6 ee 32 fe f6 7e 12 bc b6 d2 e6 ee 32 fe f6 7e 12 bc b6 d2 e6 ee 32 fe f6
  //   7e 12 bc b6 d2 e6 ee 32 fe f6 7e 12 bc b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
  //   contents of rom_3 (hex, n*v repeats v):
  //   7e 12 bc b6 d2 e6 ee 32 fe f6 7e 12 bc b6 d2 e6 ee 32 fe f6 7e 12 bc b6 d2 e6 ee 32 fe f6 7e 12 bc
  //   b6 d2 e6 ee 32 fe f6 7e 12 bc b6 d2 e6 ee 32 fe f6 7e 12 bc b6 d2 e6 ee 32 fe f6 7e 12 bc b6 d2 e6
  //   ee 32 fe f6 7e 12 bc b6 d2 e6 ee 32 fe f6 7e 12 bc b6 d2 e6 ee 32 fe f6 7e 12 bc b6 d2 e6 ee 32 fe
  //   f6 7e 12 bc b6 d2 e6 ee 32 fe f6 7e 12 bc b6 d2 e6 ee 32 fe f6 7e 12 bc b6 d2 e6 ee 32 fe f6 7e 12
  //   bc b6 d2 e6 ee 32 fe f6 7e 12 bc b6 d2 e6 ee 32 fe f6 7e 12 bc b6 d2 e6 ee 32 fe f6 7e 12 bc b6 d2
  //   e6 ee 32 fe f6 7e 12 bc b6 d2 e6 ee 32 fe f6 7e 12 bc b6 d2 e6 ee 32 fe f6 7e 12 bc b6 d2 e6 ee 32
  //   fe f6 7e 12 bc b6 d2 e6 ee 32 fe f6 7e 12 bc b6 d2 e6 ee 32 fe f6 7e 12 bc b6 d2 e6 ee 32 fe f6 7e
  //   12 bc b6 d2 e6 ee 32 fe f6 7e 12 bc b6 d2 e6 ee 32 fe f6 7e 12 bc b6 d2 e6 ee 32 fe f6 7e 12 bc b6
  //   d2 e6 ee 32 fe f6 7e 12 bc b6 d2 e6 ee 32 fe f6 7e 12 bc b6 d2 e6 ee 32 fe f6 7e 12 bc b6 d2 e6 ee
  //   32 fe f6 7e 12 bc b6 d2 e6 ee 32 fe f6 7e 12 bc b6 d2 e6 ee 32 fe f6 7e 12 bc b6 d2 e6 ee 32 fe f6
  //   7e 12 bc b6 d2 e6 ee 32 fe f6 7e 12 bc b6 d2 e6 ee 32 fe f6 7e 12 bc b6 d2 e6 ee 32 fe f6 7e 12 bc
  //   b6 d2 e6 ee 32 fe f6 7e 12 bc b6 d2 e6 ee 32 fe f6 7e 12 bc b6 d2 e6 ee 32 fe f6 7e 12 bc b6 d2 e6
  //   ee 32 fe f6 7e 12 bc b6 d2 e6 ee 32 fe f6 7e 12 bc b6 d2 e6 ee 32 fe f6 7e 12 bc b6 d2 e6 ee 32 fe
  //   f6 7e 12 bc b6 d2 e6 ee 32 fe f6 7e 12 bc b6 d2 e6 ee 32 fe f6 7e 12 bc b6 d2 e6 ee 32 fe f6 7e 12
  //   bc b6 d2 e6 ee 32 fe f6 7e 12 bc b6 d2 e6 ee 32 fe f6 7e 12 bc b6 d2 e6 ee 32 fe f6 7e 12 bc b6 d2
  //   e6 ee 32 fe f6 7e 12 bc b6 d2 e6 ee 32 fe f6 7e 12 bc b6 d2 e6 ee 32 fe f6 7e 12 bc b6 d2 e6 ee 32
  //   fe f6 7e 12 bc b6 d2 e6 ee 32 fe f6 7e 12 bc b6 d2 e6 ee 32 fe f6 7e 12 bc b6 d2 e6 ee 32 fe f6 7e
  //   12 bc b6 d2 e6 ee 32 fe f6 7e 12 bc b6 d2 e6 ee 32 fe f6 7e 12 bc b6 d2 e6 ee 32 fe f6 7e 12 bc b6
  //   d2 e6 ee 32 fe f6 7e 12 bc b6 d2 e6 ee 32 fe f6 7e 12 bc b6 d2 e6 ee 32 fe f6 7e 12 bc b6 d2 e6 ee
  //   32 fe f6 7e 12 bc b6 d2 e6 ee 32 fe f6 7e 12 bc b6 d2 e6 ee 32 fe f6 7e 12 bc b6 d2 e6 ee 32 fe f6
  //   7e 12 bc b6 d2 e6 ee 32 fe f6 7e 12 bc b6 d2 e6 ee 32 fe f6 7e 12 bc b6 d2 e6 ee 32 fe f6 7e 12 bc
  //   b6 d2 e6 ee 32 fe f6 7e 12 bc b6 d2 e6 ee 32 fe f6 7e 12 bc b6 d2 e6 ee 32 fe f6 7e 12 bc b6 d2 e6
  //   ee 32 fe f6 7e 12 bc b6 d2 e6 ee 32 fe f6 7e 12 bc b6 d2 e6 ee 32 fe f6 7e 12 bc b6 d2 e6 ee 32 fe
  //   f6 7e 12 bc b6 d2 e6 ee 32 fe f6 7e 12 bc b6 d2 e6 ee 32 fe f6 7e 12 bc b6 d2 e6 ee 32 fe f6 7e 12
  //   bc b6 d2 e6 ee 32 fe f6 7e 12 bc b6 d2 e6 ee 32 fe f6 7e 12 bc b6 d2 e6 ee 32 fe f6 7e 12 bc b6 d2
  //   e6 ee 32 fe f6 7e 12 bc b6 d2 e6 ee 32 fe f6 7e 12 bc b6 d2 e6 ee 32 fe f6 7e 12 bc b6 d2 e6 ee 32
  //   fe f6 7e 12 bc b6 d2 e6 ee 32 fe f6 7e 12 bc b6 d2 e6 ee 32 fe f6 7e 12 bc b6 d2 e6 ee 32 fe f6 7e
  //   12 bc b6 d2 e6 ee 32 fe f6 7e 12 bc b6 d2 e6 ee 32 fe f6 7e 12 bc b6 d2 e6 ee 32 fe f6 7e 12 bc b6
  //   d2 e6 ee 32 fe f6 7e 12 bc b6 d2 e6 ee 32 fe f6 7e 12 bc b6 d2 e6 ee 32 fe f6 7e 12 bc b6 d2 e6 ee
  //   32 fe f6 7e 12 bc b6 d2 e6 ee 32 fe f6 7e 12 bc b6 d2 e6 ee 32 fe f6 7e 12 bc b6 d2 e6 ee 32 fe f6
  //   7e 12 bc b6 d2 e6 ee 32 fe f6 7e 12 bc b6 d2 e6 ee 32 fe f6 7e 12 bc b6 d2 e6 ee 32 fe f6 7e 12 bc
  //   b6 d2 e6 ee 32 fe f6 7e 12 bc b6 d2 e6 ee 32 fe f6 7e 12 bc b6 d2 e6 ee 32 fe f6 7e 12 bc b6 d2 e6
  //   ee 32 fe f6 7e 12 bc b6 d2 e6 ee 32 fe f6 7e 12 bc b6 d2 e6 ee 32 fe f6 7e 12 bc b6 d2 e6 ee 32 fe
  //   f6 7e 12 bc b6 d2 e6 ee 32 fe f6 7e 12 bc b6 d2 e6 ee 32 fe f6 7e 12 bc b6 d2 e6 ee 32 fe f6 7e 12
  //   bc b6 d2 e6 ee 32 fe f6 7e 12 bc b6 d2 e6 ee 32 fe f6 7e 12 bc b6 d2 e6 ee 32 fe f6 7e 12 bc b6 d2
  //   e6 ee 32 fe f6 7e 12 bc b6 d2 e6 ee 32 fe f6 7e 12 bc b6 d2 e6 ee 32 fe f6 7e 12 bc b6 d2 e6 ee 32
  //   fe f6 7e 12 bc b6 d2 e6 ee 32 fe f6 7e 12 bc b6 d2 e6 ee 32 fe f6 7e 12 bc b6 d2 e6 ee 32 fe f6 7e
  //   12 bc b6 d2 e6 ee 32 fe f6 7e 12 bc b6 d2 e6 ee 32 fe f6 7e 12 bc b6 d2 e6 ee 32 fe f6 7e 12 bc b6
  //   d2 e6 ee 32 fe f6 7e 12 bc b6 d2 e6 ee 32 fe f6 7e 12 bc b6 d2 e6 ee 32 fe f6 7e 12 bc b6 d2 e6 ee
  //   32 fe f6 7e 12 bc b6 d2 e6 ee 32 fe f6 7e 12 bc b6 d2 e6 ee 32 fe f6 7e 12 bc b6 d2 e6 ee 32 fe f6
  //   7e 12 bc b6 d2 e6 ee 32 fe f6 7e 12 bc b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
  //   contents of rom_4 (hex, n*v repeats v):
  //   7e 12 bc b6 d2 e6 ee 32 fe f6 7e 12 bc b6 d2 e6 ee 32 fe f6 7e 12 bc b6 d2 e6 ee 32 fe f6 7e 12 bc
  //   b6 d2 e6 ee 32 fe f6 7e 12 bc b6 d2 e6 ee 32 fe f6 7e 12 bc b6 d2 e6 ee 32 fe f6 7e 12 bc b6 d2 e6
  //   ee 32 fe f6 7e 12 bc b6 d2 e6 ee 32 fe f6 7e 12 bc b6 d2 e6 ee 32 fe f6 7e 12 bc b6 d2 e6 ee 32 fe
  //   f6 7e 12 bc b6 d2 e6 ee 32 fe f6 7e 12 bc b6 d2 e6 ee 32 fe f6 7e 12 bc b6 d2 e6 ee 32 fe f6 7e 12
  //   bc b6 d2 e6 ee 32 fe f6 7e 12 bc b6 d2 e6 ee 32 fe f6 7e 12 bc b6 d2 e6 ee 32 fe f6 7e 12 bc b6 d2
  //   e6 ee 32 fe f6 7e 12 bc b6 d2 e6 ee 32 fe f6 7e 12 bc b6 d2 e6 ee 32 fe f6 7e 12 bc b6 d2 e6 ee 32
  //   fe f6 7e 12 bc b6 d2 e6 ee 32 fe f6 7e 12 bc b6 d2 e6 ee 32 fe f6 7e 12 bc b6 d2 e6 ee 32 fe f6 7e
  //   12 bc b6 d2 e6 ee 32 fe f6 7e 12 bc b6 d2 e6 ee 32 fe f6 7e 12 bc b6 d2 e6 ee 32 fe f6 7e 12 bc b6
  //   d2 e6 ee 32 fe f6 7e 12 bc b6 d2 e6 ee 32 fe f6 7e 12 bc b6 d2 e6 ee 32 fe f6 7e 12 bc b6 d2 e6 ee
  //   32 fe f6 7e 12 bc b6 d2 e6 ee 32 fe f6 7e 12 bc b6 d2 e6 ee 32 fe f6 7e 12 bc b6 d2 e6 ee 32 fe f6
  //   7e 12 bc b6 d2 e6 ee 32 fe f6 7e 12 bc b6 d2 e6 ee 32 fe f6 7e 12 bc b6 d2 e6 ee 32 fe f6 7e 12 bc
  //   b6 d2 e6 ee 32 fe f6 7e 12 bc b6 d2 e6 ee 32 fe f6 7e 12 bc b6 d2 e6 ee 32 fe f6 7e 12 bc b6 d2 e6
  //   ee 32 fe f6 7e 12 bc b6 d2 e6 ee 32 fe f6 7e 12 bc b6 d2 e6 ee 32 fe f6 7e 12 bc b6 d2 e6 ee 32 fe
  //   f6 7e 12 bc b6 d2 e6 ee 32 fe f6 7e 12 bc b6 d2 e6 ee 32 fe f6 7e 12 bc b6 d2 e6 ee 32 fe f6 7e 12
  //   bc b6 d2 e6 ee 32 fe f6 7e 12 bc b6 d2 e6 ee 32 fe f6 7e 12 bc b6 d2 e6 ee 32 fe f6 7e 12 bc b6 d2
  //   e6 ee 32 fe f6 7e 12 bc b6 d2 e6 ee 32 fe f6 7e 12 bc b6 d2 e6 ee 32 fe f6 7e 12 bc b6 d2 e6 ee 32
  //   fe f6 7e 12 bc b6 d2 e6 ee 32 fe f6 7e 12 bc b6 d2 e6 ee 32 fe f6 7e 12 bc b6 d2 e6 ee 32 fe f6 7e
  //   12 bc b6 d2 e6 ee 32 fe f6 7e 12 bc b6 d2 e6 ee 32 fe f6 7e 12 bc b6 d2 e6 ee 32 fe f6 7e 12 bc b6
  //   d2 e6 ee 32 fe f6 7e 12 bc b6 d2 e6 ee 32 fe f6 7e 12 bc b6 d2 e6 ee 32 fe f6 7e 12 bc b6 d2 e6 ee
  //   32 fe f6 7e 12 bc b6 d2 e6 ee 32 fe f6 7e 12 bc b6 d2 e6 ee 32 fe f6 7e 12 bc b6 d2 e6 ee 32 fe f6
  //   7e 12 bc b6 d2 e6 ee 32 fe f6 7e 12 bc b6 d2 e6 ee 32 fe f6 7e 12 bc b6 d2 e6 ee 32 fe f6 7e 12 bc
  //   b6 d2 e6 ee 32 fe f6 7e 12 bc b6 d2 e6 ee 32 fe f6 7e 12 bc b6 d2 e6 ee 32 fe f6 7e 12 bc b6 d2 e6
  //   ee 32 fe f6 7e 12 bc b6 d2 e6 ee 32 fe f6 7e 12 bc b6 d2 e6 ee 32 fe f6 7e 12 bc b6 d2 e6 ee 32 fe
  //   f6 7e 12 bc b6 d2 e6 ee 32 fe f6 7e 12 bc b6 d2 e6 ee 32 fe f6 7e 12 bc b6 d2 e6 ee 32 fe f6 7e 12
  //   bc b6 d2 e6 ee 32 fe f6 7e 12 bc b6 d2 e6 ee 32 fe f6 7e 12 bc b6 d2 e6 ee 32 fe f6 7e 12 bc b6 d2
  //   e6 ee 32 fe f6 7e 12 bc b6 d2 e6 ee 32 fe f6 7e 12 bc b6 d2 e6 ee 32 fe f6 7e 12 bc b6 d2 e6 ee 32
  //   fe f6 7e 12 bc b6 d2 e6 ee 32 fe f6 7e 12 bc b6 d2 e6 ee 32 fe f6 7e 12 bc b6 d2 e6 ee 32 fe f6 7e
  //   12 bc b6 d2 e6 ee 32 fe f6 7e 12 bc b6 d2 e6 ee 32 fe f6 7e 12 bc b6 d2 e6 ee 32 fe f6 7e 12 bc b6
  //   d2 e6 ee 32 fe f6 7e 12 bc b6 d2 e6 ee 32 fe f6 7e 12 bc b6 d2 e6 ee 32 fe f6 7e 12 bc b6 d2 e6 ee
  //   32 fe f6 7e 12 bc b6 d2 e6 ee 32 fe f6 7e 12 bc b6 d2 e6 ee 32 fe f6 7e 12 bc b6 d2 e6 ee 32 fe f6
  //   7e 12 bc b6 d2 e6 ee 32 fe f6 7e 12 bc b6 d2 e6 ee 32 fe f6 7e 12 bc b6 d2 e6 ee 32 fe f6 7e 12 bc
  //   b6 d2 e6 ee 32 fe f6 7e 12 bc b6 d2 e6 ee 32 fe f6 7e 12 bc b6 d2 e6 ee 32 fe f6 7e 12 bc b6 d2 e6
  //   ee 32 fe f6 7e 12 bc b6 d2 e6 ee 32 fe f6 7e 12 bc b6 d2 e6 ee 32 fe f6 7e 12 bc b6 d2 e6 ee 32 fe
  //   f6 7e 12 bc b6 d2 e6 ee 32 fe f6 7e 12 bc b6 d2 e6 ee 32 fe f6 7e 12 bc b6 d2 e6 ee 32 fe f6 7e 12
  //   bc b6 d2 e6 ee 32 fe f6 7e 12 bc b6 d2 e6 ee 32 fe f6 7e 12 bc b6 d2 e6 ee 32 fe f6 7e 12 bc b6 d2
  //   e6 ee 32 fe f6 7e 12 bc b6 d2 e6 ee 32 fe f6 7e 12 bc b6 d2 e6 ee 32 fe f6 7e 12 bc b6 d2 e6 ee 32
  //   fe f6 7e 12 bc b6 d2 e6 ee 32 fe f6 7e 12 bc b6 d2 e6 ee 32 fe f6 7e 12 bc b6 d2 e6 ee 32 fe f6 7e
  //   12 bc b6 d2 e6 ee 32 fe f6 7e 12 bc b6 d2 e6 ee 32 fe f6 7e 12 bc b6 d2 e6 ee 32 fe f6 7e 12 bc b6
  //   d2 e6 ee 32 fe f6 7e 12 bc b6 d2 e6 ee 32 fe f6 7e 12 bc b6 d2 e6 ee 32 fe f6 7e 12 bc b6 d2 e6 ee
  //   32 fe f6 7e 12 bc b6 d2 e6 ee 32 fe f6 7e 12 bc b6 d2 e6 ee 32 fe f6 7e 12 bc b6 d2 e6 ee 32 fe f6
  //   7e 12 bc b6 d2 e6 ee 32 fe f6 7e 12 bc b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
  //   contents of rom_5 (hex, n*v repeats v):
  //   7e 12 bc b6 d2 e6 ee 32 fe f6 7e 12 bc b6 d2 e6 ee 32 fe f6 7e 12 bc b6 d2 e6 ee 32 fe f6 7e 12 bc
  //   b6 d2 e6 ee 32 fe f6 7e 12 bc b6 d2 e6 ee 32 fe f6 7e 12 bc b6 d2 e6 ee 32 fe f6 7e 12 bc b6 d2 e6
  //   ee 32 fe f6 7e 12 bc b6 d2 e6 ee 32 fe f6 7e 12 bc b6 d2 e6 ee 32 fe f6 7e 12 bc b6 d2 e6 ee 32 fe
  //   f6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
endmodule

module REGS (
  input  [15:0] D,
  input  IE,
  input  CLK,
  input  OE,
  input  R,
  output [15:0] out_6,
  output [15:0] O
);

  Register #(.width(16)) register_1 (.D(D), .en(IE), .clk(CLK), .Q(out_6), .clr(R));
  assign O = OE ? out_6 : 16'bz;  // Controlled_Buffer controlled_buffer_1
endmodule

module COUNT (
  input  R,
  input  [3:0] JInEO,
  input  CLK,
  input  [15:0] D,
  output [15:0] Q
);

  wire not_1_out;
  wire [15:0] counter_1_q;

  not not_1 (not_1_out, JInEO[1]);
  Counter #(.max('hffff), .width(16)) counter_1 (
    .clr(R), .load(JInEO[0]), .up(not_1_out), .count(JInEO[2]), .clk(CLK), .D(D), .Q(counter_1_q));  // open: carry
  assign Q = JInEO[3] ? counter_1_q : 16'bz;  // Controlled_Buffer controlled_buffer_1
endmodule

module ALU (
  input  [15:0] A,
  input  [15:0] B,
  input  [1:0] AB,
  input  [6:0] Sel,
  output [15:0] Q,
  output [6:0] Flags
);

  wire [15:0] adder_1_out, divider_1_out, lgc_1_out_4, multiplexer_1_out, multiplexer_2_out,
       multiplier_1_out, shft_1_q, subtractor_1_out;

  Multiplexer #(.select(2), .width(16)) multiplexer_1 (
    .in0(A), .in1(A), .in2(B), .in3(B), .out(multiplexer_1_out), .sel(AB));
  Multiplexer #(.select(2), .width(16)) multiplexer_2 (
    .in0(B), .in1(A), .in2(B), .in3(A), .out(multiplexer_2_out), .sel(AB));
  SHFT shft_1 (.D(multiplexer_1_out), .Sel(Sel[6:5]), .Q(shft_1_q), .SHC(Flags[2]));
  LGC lgc_1 (.B(multiplexer_2_out), .A(multiplexer_1_out), .Sel(Sel[4:2]), .out_4(lgc_1_out_4), .F(Flags[6:3]));
  Adder #(.width(16)) adder_1 (.a(shft_1_q), .b(lgc_1_out_4), .out(adder_1_out), .cout(Flags[1]));  // open: cin
  Subtractor #(.width(16)) subtractor_1 (.a(shft_1_q), .b(lgc_1_out_4), .out(subtractor_1_out));  // open: bin, bout
  Multiplier #(.width(16)) multiplier_1 (.a(shft_1_q), .b(lgc_1_out_4), .out(multiplier_1_out));  // open: cin, cout
  Divider #(.width(16)) divider_1 (.a(shft_1_q), .b(lgc_1_out_4), .out(divider_1_out));  // open: upper, rem
  Multiplexer #(.select(2), .width(16)) multiplexer_3 (
    .in0(adder_1_out), .in1(subtractor_1_out), .in2(multiplier_1_out), .in3(divider_1_out), .out(Q),
    .sel(Sel[1:0]));
  Comparator #(.width(16)) comparator_1 (.a({16{1'b0}}), .b(Q), .eq(Flags[0]));  // open: gt, lt
endmodule

module SHFT (
  input  [15:0] D,
  input  [1:0] Sel,
  output [15:0] Q,
  output SHC
);

  Multiplexer #(.select(2), .width(16)) multiplexer_1 (
    .in0(D), .in1({16{1'b0}}), .in2({D[14:0], 1'b0}), .in3({1'b0, D[15:1]}), .out(Q), .sel(Sel));

  assign SHC = D[15];
endmodule

module LGC (
  input  [15:0] B,
  input  [15:0] A,
  input  [2:0] Sel,
  output [15:0] out_4,
  output [3:0] F
);

  wire [3:0] comparator_1_eq;
  wire [15:0] and_1_out, demultiplexer_1_out0, demultiplexer_1_out3, demultiplexer_1_out4,
       demultiplexer_1_out5, demultiplexer_1_out6, demultiplexer_1_out7, demultiplexer_2_out4,
       demultiplexer_2_out5, demultiplexer_2_out6, demultiplexer_2_out7, not_2_out, or_1_out, xor_1_out;

  Demultiplexer #(.select(3), .width(16)) demultiplexer_1 (
    .out0(demultiplexer_1_out0), .out3(demultiplexer_1_out3), .out4(demultiplexer_1_out4),
    .out5(demultiplexer_1_out5), .out6(demultiplexer_1_out6), .out7(demultiplexer_1_out7), .in(B), .sel(Sel));  // open: out1, out2
  Demultiplexer #(.select(3), .width(16)) demultiplexer_2 (
    .out4(demultiplexer_2_out4), .out5(demultiplexer_2_out5), .out6(demultiplexer_2_out6),
    .out7(demultiplexer_2_out7), .in(A), .sel(Sel));  // open: out0, out1, out2, out3
  assign and_1_out = demultiplexer_1_out4 & demultiplexer_2_out4;  // AND_Gate and_1, 16 bits wide
  assign or_1_out = demultiplexer_1_out5 | demultiplexer_2_out5;  // OR_Gate or_1, 16 bits wide
  Comparator #(.width(16)) comparator_1 (
    .a(demultiplexer_1_out7), .b(demultiplexer_2_out7), .gt(comparator_1_eq[2]), .eq(comparator_1_eq[0]),
    .lt(comparator_1_eq[3]));
  assign xor_1_out = demultiplexer_1_out6 ^ demultiplexer_2_out6;  // XOR_Gate xor_1, 16 bits wide
  not not_1 (comparator_1_eq[1], comparator_1_eq[0]);
  assign not_2_out = ~demultiplexer_1_out3;  // NOT_Gate not_2, 16 bits wide
  Multiplexer #(.select(3), .width(16)) multiplexer_1 (
    .in0(demultiplexer_1_out0), .in1({16{1'b0}}), .in2(16'h1), .in3(not_2_out), .in4(and_1_out),
    .in5(or_1_out), .in6(xor_1_out), .out(out_4), .sel(Sel));  // open: in7
  Multiplexer #(.width(4)) multiplexer_2 (.in0(4'b0001), .in1(comparator_1_eq), .out(F), .sel(Sel[2]));
endmodule

module Console (
  input  OE,
  input  [15:0] D,
  input  IE,
  input  CLK,
  input  SP,
  input  R,
  input  Push
);

  wire [7:0] multiplexer_1_out;
  wire [15:0] register_1_q;

  Register #(.width(16)) register_1 (.D(D), .en(IE), .clk(CLK), .Q(register_1_q), .clr(R));
  Multiplexer #(.width(8)) multiplexer_1 (
    .in0(register_1_q[7:0]), .in1(register_1_q[15:8]), .out(multiplexer_1_out), .sel(SP));
  TTY tty_1 (.data(multiplexer_1_out[6:0]), .clk(CLK), .we(Push), .clr(R));
  assign D = OE ? {{8{1'b0}}, multiplexer_1_out} : 16'bz;  // Controlled_Buffer controlled_buffer_1
endmodule

module CC (
  input  nCLK,
  input  R,
  output [2:0] Q
);

  wire counter_1_carry, not_1_out, or_1_out;

  or or_1 (or_1_out, R, counter_1_carry);
  Counter #(.max('h7), .width(3)) counter_1 (
    .clr(or_1_out), .clk(not_1_out), .carry(counter_1_carry), .Q(Q));  // open: load, up, count, D
  not not_1 (not_1_out, nCLK);
endmodule

module CU (
  input  [2:0] T,
  input  [7:0] I,
  input  [6:0] F,
  output [6:0] QALU,
  output [24:0] Q1,
  output [7:0] Q2
);

  ROM #(.addrWidth(20)) rom_1 (.addr({F, 2'b00, I, T}), .data({Q1[0], QALU}));
  ROM #(.addrWidth(20)) rom_2 (.addr({F, 2'b01, I, T}), .data(Q1[8:1]));
  ROM #(.addrWidth(20)) rom_3 (.addr({F, 2'b10, I, T}), .data(Q1[16:9]));
  ROM #(.addrWidth(20)) rom_4 (.addr({F, 2'b11, I, T}), .data(Q1[24:17]));
  ROM #(.addrWidth(20)) rom_5 (.addr({F, 2'b00, I, T}), .data(Q2));

  // Notes on the sheet:
  //   contents of rom_1 (hex, n*v repeats v):
  //   42*0 80 7*0 80 7*0 80 7*0 80 7*0 81 7*0 81 7*0 82 7*0 82 7*0 82 7*0 83 7*0 83 7*0 ac 7*0 ac 7*0 90
  //   7*0 90 7*0 94 7*0 94 7*0 98 7*0 98 7*0 98 7*0 98 7*0 e4 7*0 e4 7*0 c4 7*0 c4 7*0 9c 7*0 9c 215*0 88
  //   7*0 88 7*0 89 7*0 89 39*0 84 7*0 84 23*0 82 1498*0 2 7*0 8 7*0 4 7*0 10 4*0 3 7*0 23 7*0 49 7*0 69
  //   7*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
  //   contents of rom_2 (hex, n*v repeats v):
  //   42*0 80 7*0 80 7*0 80 7*0 80 7*0 81 7*0 81 7*0 82 7*0 82 7*0 82 7*0 83 7*0 83 7*0 ac 7*0 ac 7*0 90
  //   7*0 90 7*0 94 7*0 94 7*0 98 7*0 98 7*0 98 7*0 98 7*0 e4 7*0 e4 7*0 c4 7*0 c4 7*0 9c 7*0 9c 215*0 88
  //   7*0 88 7*0 89 7*0 89 39*0 84 7*0 84 23*0 82 1498*0 2 7*0 8 7*0 4 7*0 10 4*0 3 7*0 23 7*0 49 7*0 69
  //   7*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
  //   contents of rom_3 (hex, n*v repeats v):
  //   42*0 80 7*0 80 7*0 80 7*0 80 7*0 81 7*0 81 7*0 82 7*0 82 7*0 82 7*0 83 7*0 83 7*0 ac 7*0 ac 7*0 90
  //   7*0 90 7*0 94 7*0 94 7*0 98 7*0 98 7*0 98 7*0 98 7*0 e4 7*0 e4 7*0 c4 7*0 c4 7*0 9c 7*0 9c 215*0 88
  //   7*0 88 7*0 89 7*0 89 39*0 84 7*0 84 23*0 82 1498*0 2 7*0 8 7*0 4 7*0 10 4*0 3 7*0 23 7*0 49 7*0 69
  //   7*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
  //   contents of rom_4 (hex, n*v repeats v):
  //   42*0 80 7*0 80 7*0 80 7*0 80 7*0 81 7*0 81 7*0 82 7*0 82 7*0 82 7*0 83 7*0 83 7*0 ac 7*0 ac 7*0 90
  //   7*0 90 7*0 94 7*0 94 7*0 98 7*0 98 7*0 98 7*0 98 7*0 e4 7*0 e4 7*0 c4 7*0 c4 7*0 9c 7*0 9c 215*0 88
  //   7*0 88 7*0 89 7*0 89 39*0 84 7*0 84 23*0 82 1498*0 2 7*0 8 7*0 4 7*0 10 4*0 3 7*0 23 7*0 49 7*0 69
  //   7*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
  //   contents of rom_5 (hex, n*v repeats v):
  //   11*0 2 4 6*0 2 4 6*0 2 4 6*0 2 4 253*0 2 0 0 4 124*0 1 192*0 8 7*0 8 7583*0 2 4 6*0 2 4 6*0 2 4 6*0
  //   2 4 253*0 2 0 0 4 124*0 1 192*0 8 7*0 8 7583*0 2 4 6*0 2 4 6*0 2 4 6*0 2 4 253*0 2 0 0 4 124*0 1
  //   192*0 8 7*0 8 7583*0 2 4 6*0 2 4 6*0 2 4 6*0 2 4 253*0 2 0 0 4 124*0 1 192*0 8 7*0 8 7583*0 2 4 6*0
  //   2 4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
endmodule
